# Fritzing sketch PWM_Diode (saved by Fritzing 0.9.0b)
breadboards: 1

parts:
  Part1 = Arduino Uno (Rev3)
  LED1 = LED - 5mm [color="Red (633nm)" package="5 mm [THT]"]
  R3 = Resistor [tolerance=±5% resistance=10k package=THT]

nets:
  N1: Part1.D9_PWM, LED1.anode, R3.Pin_0, R3.Pin_1
  N2: Part1.GND, LED1.cathode
